// Logisim project ALU.circ as structural Verilog: 1 circuit, main circuit main
module main (
  input  A2,
  input  A1,
  input  B2,
  input  A0,
  input  B1,
  input  A3,
  input  B0,
  input  B3,
  input  OP,
  output S2,
  output S1,
  output S0,
  output S3,
  output out_14,
  output out_15,
  output out_16,
  output C4,
  output out_18,
  output F0,
  output F1,
  output F2,
  output F3
);

  wire AND0_out, AND1_out, AND2_out, AND3_out, and_2_out, and_3_out, and_4_out, and_5_out, and_6_out,
       and_7_out, xor_2_out, xor_4_out, xor_6_out;

  and AND0 (AND0_out, B0, A0);
  xor xor_1 (S0, A0, B0);
  and and_1 (out_14, A0, B0);
  xor xor_2 (xor_2_out, A1, B1);
  and and_2 (and_2_out, A1, B1);
  and and_3 (and_3_out, xor_2_out, out_14);
  and AND1 (AND1_out, B1, A1);
  xor xor_3 (S1, xor_2_out, out_14);
  or or_1 (out_15, and_3_out, and_2_out);
  xor xor_4 (xor_4_out, A2, B2);
  and and_4 (and_4_out, A2, B2);
  and AND2 (AND2_out, B2, A2);
  xor xor_5 (S2, xor_4_out, out_15);
  and and_5 (and_5_out, xor_4_out, out_15);
  or or_2 (out_16, and_5_out, and_4_out);
  xor xor_6 (xor_6_out, A3, B3);
  and and_6 (and_6_out, A3, B3);
  and AND3 (AND3_out, B3, A3);
  xor xor_7 (S3, xor_6_out, out_16);
  and and_7 (and_7_out, xor_6_out, out_16);
  or or_3 (C4, and_7_out, and_6_out);
  and and_8 (out_18, C4, OP);
  Multiplexer multiplexer_1 (.in0(AND3_out), .in1(S3), .out(F3), .sel(OP));
  Multiplexer multiplexer_2 (.in0(AND2_out), .in1(S2), .out(F2), .sel(OP));
  Multiplexer multiplexer_3 (.in0(AND1_out), .in1(S1), .out(F1), .sel(OP));
  Multiplexer multiplexer_4 (.in0(AND0_out), .in1(S0), .out(F0), .sel(OP));
endmodule
