// Logisim project FourBitRippleAdder.circ as structural Verilog: 1 circuit, main circuit main
module main (
  input  A2,
  input  A1,
  input  B2,
  input  A0,
  input  B1,
  input  A3,
  input  B0,
  input  B3,
  output S2,
  output S1,
  output S0,
  output S3,
  output C4
);

  wire and_1_out, and_2_out, and_3_out, and_4_out, and_5_out, and_6_out, and_7_out, or_1_out, or_2_out,
       xor_2_out, xor_4_out, xor_6_out;

  xor xor_1 (S0, A0, B0);
  and and_1 (and_1_out, A0, B0);
  xor xor_2 (xor_2_out, A1, B1);
  and and_2 (and_2_out, A1, B1);
  xor xor_3 (S1, xor_2_out, and_1_out);
  and and_3 (and_3_out, xor_2_out, and_1_out);
  or or_1 (or_1_out, and_3_out, and_2_out);
  xor xor_4 (xor_4_out, A2, B2);
  and and_4 (and_4_out, A2, B2);
  xor xor_5 (S2, xor_4_out, or_1_out);
  and and_5 (and_5_out, xor_4_out, or_1_out);
  or or_2 (or_2_out, and_5_out, and_4_out);
  xor xor_6 (xor_6_out, A3, B3);
  and and_6 (and_6_out, A3, B3);
  xor xor_7 (S3, xor_6_out, or_2_out);
  and and_7 (and_7_out, xor_6_out, or_2_out);
  or or_3 (C4, and_7_out, and_6_out);

  // Notes on the sheet:
  //   Line 257 on the Truth Table
endmodule
