// Logisim project FullAdder.circ as structural Verilog: 1 circuit, main circuit main
module main (
  input  CIN,
  input  A,
  input  B,
  output SUM,
  output COUT
);

  wire A1_out, A2_out, A3_out, A4_out, N1_out, N2_out, X1_out;

  xor X1 (X1_out, A, B);
  and A4 (A4_out, A, B);
  not N1 (N1_out, X1_out);
  not N2 (N2_out, CIN);
  and A1 (A1_out, CIN, N1_out);
  and A2 (A2_out, N2_out, X1_out);
  and A3 (A3_out, CIN, X1_out);
  or O1 (SUM, A1_out, A2_out);
  or O2 (COUT, A3_out, A4_out);
endmodule
