// Logisim project FullAdderNAND.circ as structural Verilog: 1 circuit, main circuit main
module main (
  input  CIN,
  input  A,
  input  B,
  output SUM,
  output COUT
);

  wire NA1_out, NA2_out, NA4_out, NA5_out, NA6_out, NA7_out, NA8_out, NA9_out, NA10_out, NA11_out, NA12_out;

  nand NA4 (NA4_out, B, B);
  nand NA5 (NA5_out, A, A);
  nand NA1 (NA1_out, B, A);
  nand NA6 (NA6_out, A, NA4_out);
  nand NA7 (NA7_out, NA5_out, B);
  nand NA8 (NA8_out, NA6_out, NA7_out);
  nand NA11 (NA11_out, CIN, NA9_out);
  nand NA9 (NA9_out, NA8_out, NA8_out);
  nand NA10 (NA10_out, CIN, CIN);
  nand NA12 (NA12_out, NA10_out, NA8_out);
  nand NA13 (SUM, NA11_out, NA12_out);
  nand NA2 (NA2_out, CIN, NA8_out);
  nand NA3 (COUT, NA2_out, NA1_out);
endmodule
