// Logisim project HalfAdder.circ as structural Verilog: 1 circuit, main circuit main
module main (
  input  A,
  input  B,
  output Sum,
  output Carry
);

  wire A2_out, A3_out, N1_out, N2_out;

  and A1 (Sum, A, B);
  not N1 (N1_out, B);
  not N2 (N2_out, A);
  and A2 (A2_out, A, N1_out);
  and A3 (A3_out, N2_out, B);
  or O1 (Carry, A2_out, A3_out);
endmodule
