// Logisim project HalfAdderNAND.circ as structural Verilog: 1 circuit, main circuit main
module main (
  input  A,
  input  B,
  output Sum,
  output Carry
);

  wire NA1_out, NA2_out, NA4_out, NA5_out, NA6_out;

  nand NA1 (NA1_out, B, B);
  nand NA4 (NA4_out, A, A);
  nand NA6 (NA6_out, A, B);
  nand NA2 (NA2_out, A, NA1_out);
  nand NA5 (NA5_out, NA4_out, B);
  nand NA7 (Carry, NA6_out, NA6_out);
  nand NA3 (Sum, NA2_out, NA5_out);
endmodule
